# Fritzing sketch TB1-HOLA MUNDO (saved by Fritzing 0.9.3b)
breadboards: 2

parts:
  CHI035A1 = CHI035A2 [package="DIP (Dual Inline) [THT]"]
  VCC1 = Pack de pilas 3xAA  # not connected
  R2 = Resistor [tolerance=±5% resistance=220 package=THT]
  LED1 = LED - 5mm [color="Red (633nm)" package="5 mm [THT]"]

nets:
  N1: CHI035A1.pin14, LED1.cathode
  N2: R2.Pin_1, LED1.anode

custom parts:
  CHI035A2: PICAXE CHI035A Entradas: terminales verdes Salidas: terminales rojos Alimentación: terminal gris Salidas directas: pines macho
  Pack de pilas 3xAA: Standard 3x AA battery pack (4,5 Volts)
